# Fritzing sketch NodeMCU32_schematic (saved by Fritzing 1.0.0rc)
breadboards: 1

parts:
  SP1 = SPEAKER [package=pcb_mount_speaker]
  CPU1 = NodeMCU WROOM ESP 32

nets:
  N1: SP1.+, CPU1.pin_18
  N2: SP1.-, CPU1.pin_30
  N3: CPU1.pin_8, CPU1.pin_24, CPU1.pin_28
  N4: CPU1.pin_9, CPU1.pin_25

custom parts:
  NodeMCU WROOM ESP 32: 30 pol Development Kit
