# Fritzing sketch NodeMCU32b_schematic (saved by Fritzing 1.0.0rc)
breadboards: 1

parts:
  SP1 = SPEAKER [package=pcb_mount_speaker]
  esp1 = ESP32 DevKitc V4

nets:
  N1: SP1.+, esp1.GND
  N2: SP1.-, esp1.IO22
  N3: esp1.CLK, esp1.D0

custom parts:
  ESP32 DevKitc V4: ESP32-DevKitC board with ESP32-WROOM-32 module. ESP32-DevKitC V4 is a small-sized ESP32-based development board produced by Espressif. Most of the pins on the ESP module are broken out to the pin headers on the board. The pins D0, D1, D2, D3, CMD and CLK are used internally for communication between ESP32 and SPI flash memory. They are grouped on both sides near the USB connector. Avoid using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
