# Fritzing sketch NodeMCU_schematic (saved by Fritzing 1.0.0rc)
breadboards: 1

parts:
  SP1 = SPEAKER [package=pcb_mount_speaker]
  Mod1 = Amica NodeMCU DEVKIT 1.0

nets:
  N1: SP1.+, Mod1.pin2, Mod1.pin_9, Mod1.pin_25, Mod1.pin_29
  N2: SP1.-, Mod1.pin4
  N3: Mod1.pin1, Mod1.pin_10, Mod1.pin_26
