# Fritzing sketch Wemos_schematic3 (saved by Fritzing 1.0.0rc)
breadboards: 1

parts:
  SP1 = SPEAKER [package=pcb_mount_speaker]  # not connected
  WeMos_D1_Mini1 = WeMos D1 Mini
  M1 = PAM8403 Stereo Amplifier with Volume Control [part_number=HW-012]

nets:
  N1: WeMos_D1_Mini1.5V, M1.LOUT+, M1.POWER+
  N2: WeMos_D1_Mini1.G, M1.POWER-
  N3: WeMos_D1_Mini1.RX, M1.LOUT-

custom parts:
  PAM8403 Stereo Amplifier with Volume Control: PAM8403 stereo amplifier module with volume control Descriptive words Links: PAM8403 product datasheet
