# Fritzing sketch esp8266_schematic (saved by Fritzing 1.0.0rc)
breadboards: 1

parts:
  SP1 = SPEAKER [package=pcb_mount_speaker]
  ESP8266_01 = ESP8266 ESP-01 Upgraded WiFi Module [part_number=ESP8266]

nets:
  N1: SP1.+, ESP8266_01.GND
  N2: SP1.-, ESP8266_01.RXD
  N3: ESP8266_01.VCC, ESP8266_01.CH_PD

custom parts:
  ESP8266 ESP-01 Upgraded WiFi Module: Upgraded Version ESP-01,all Flash are upgraded to 1M byte.Also support Cloud service remote transmission.
